# Fritzing sketch Port-E-schema (saved by Fritzing 0.9.6b)
breadboards: 1

parts:
  Part1 = Arduino Uno (Rev3) - ICSP
  WeMos_D1_Mini_Relay_Shield_V1 = WeMos D1 Mini Relay Shield V2  # not connected
  L1 = Solenoid  # not connected
  Part2 = PN532 Elechouse RFID NFC Module V3  # not connected
  J2 = Power Jack [package=power_jack_combo]  # not connected
  Mod1 = Amica NodeMCU DevKit 1.0
  J1 = Piezo Speaker

nets:
  N1: Part1.D6_PWM, Mod1.pin_14
  N2: Part1.D7, Mod1.pin_13
  N3: Mod1.pin1, Mod1.pin_10, Mod1.pin_26
  N4: Mod1.pin2, Mod1.pin_9, Mod1.pin_25, Mod1.pin_29, J1.pin1
  N5: Mod1.pin5, J1.pin2

custom parts:
  PN532 Elechouse RFID NFC Module V3: NFC is a popular technology in recent years. We often heard this work while smart phone company such as Samsung or HTC introduces their latest high-end phones. Almost all the high-end phone in the market support NFC. Near field communication (NFC) is a set of standards for smart phones and similar devices to establish radio communication with each other by touching them together or bringing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
  Amica NodeMCU DevKit 1.0: Amica NodeMCU DevKit 1.0 Development Kit based on ESP8266 ESP-12E, integating GPIO, PWM, IIC, 1-Wire and ADC all in one board. Links: NodeMCU information page Github
